// Logisim project 5var.circ as structural Verilog: 1 circuit, main circuit main
module main (
  input  A,
  input  B,
  input  C,
  input  D,
  input  E,
  input  [1:0] x1_x2,
  output \output 
);

  wire and_1_out, and_2_out, and_3_out, and_4_out, not_1_out, not_2_out, not_3_out, or_1_out, or_2_out,
       or_3_out;

  not not_1 (not_1_out, E);
  not not_2 (not_2_out, D);
  not not_3 (not_3_out, C);
  and and_1 (and_1_out, not_3_out, E);
  and and_2 (and_2_out, C, D, not_1_out);
  and and_3 (and_3_out, C, not_2_out);
  and and_4 (and_4_out, not_3_out, D);
  or or_1 (or_1_out, not_3_out, not_1_out);
  or or_2 (or_2_out, and_1_out, and_2_out);
  or or_3 (or_3_out, and_3_out, and_4_out);
  Multiplexer #(.select(2)) multiplexer_1 (
    .in0(or_1_out), .in1(or_2_out), .in2(or_3_out), .in3(1'b0), .out(\output ), .sel(x1_x2));  // open: en

  // Notes on the sheet:
  //   x5 x4 x3
endmodule
