// Logisim project digital-L07-counter.circ as structural Verilog: 1 circuit, main circuit main
module main (
  input  in_1
);

  wire and_1_out, and_2_out, and_3_out, and_4_out, clock_1_out, t_ff_1_qn, t_ff_2_q, t_ff_3_qn, t_ff_4_qn,
       t_ff_5_q, t_ff_6_qn, t_ff_8_q, t_ff_9_qn;

  Clock clock_1 (.out(clock_1_out));
  T_Flip_Flop t_ff_1 (.clk(clock_1_out), .T(in_1), .Qn(t_ff_1_qn));  // open: Q, preset, reset, en
  T_Flip_Flop t_ff_2 (.clk(clock_1_out), .T(in_1), .Q(t_ff_2_q));  // open: Qn, preset, reset, en
  T_Flip_Flop t_ff_3 (.clk(clock_1_out), .T(in_1), .Qn(t_ff_3_qn));  // open: Q, preset, reset, en
  T_Flip_Flop t_ff_4 (.clk(t_ff_1_qn), .T(in_1), .Qn(t_ff_4_qn));  // open: Q, preset, reset, en
  T_Flip_Flop t_ff_5 (.clk(clock_1_out), .T(t_ff_2_q), .Q(t_ff_5_q));  // open: Qn, preset, reset, en
  and and_1 (and_1_out, t_ff_5_q, t_ff_2_q);
  T_Flip_Flop t_ff_6 (.clk(clock_1_out), .T(t_ff_3_qn), .Qn(t_ff_6_qn));  // open: Q, preset, reset, en
  and and_2 (and_2_out, t_ff_6_qn, t_ff_3_qn);
  T_Flip_Flop t_ff_7 (.clk(t_ff_4_qn), .T(in_1));  // open: Q, Qn, preset, reset, en
  T_Flip_Flop t_ff_8 (.clk(clock_1_out), .T(and_1_out), .Q(t_ff_8_q));  // open: Qn, preset, reset, en
  T_Flip_Flop t_ff_9 (.clk(clock_1_out), .T(and_2_out), .Qn(t_ff_9_qn));  // open: Q, preset, reset, en
  T_Flip_Flop t_ff_10 (.clk(clock_1_out), .T(and_3_out));  // open: Q, Qn, preset, reset, en
  and and_3 (and_3_out, t_ff_8_q, and_1_out);
  T_Flip_Flop t_ff_11 (.clk(clock_1_out), .T(and_4_out));  // open: Q, Qn, preset, reset, en
  and and_4 (and_4_out, t_ff_9_qn, and_2_out);

  // Notes on the sheet:
  //   Up counter (asynchronous)
  //   Up counter (synchronous)
  //   Down counter (synchronous)
endmodule
