// Logisim project digital-L07-register.circ as structural Verilog: 1 circuit, main circuit main
module main (
  input  in_1,
  input  in_2,
  input  in_3,
  input  in_4,
  output out_5,
  output out_6,
  output out_7
);

  wire clock_1_out, d_ff_1_q, d_ff_2_q, d_ff_3_q, t_ff_1_q;

  nor nor_1 (out_5, in_1, out_6);
  nor nor_2 (out_6, out_5, in_2);
  Clock clock_1 (.out(clock_1_out));
  D_Flip_Flop d_ff_1 (.clk(clock_1_out), .D(in_3), .Q(d_ff_1_q));  // open: Qn, preset, en, reset
  T_Flip_Flop t_ff_1 (.clk(clock_1_out), .T(in_4), .Q(t_ff_1_q));  // open: Qn, preset, reset, en
  D_Flip_Flop d_ff_2 (.clk(clock_1_out), .D(d_ff_1_q), .Q(d_ff_2_q));  // open: Qn, preset, en, reset
  D_Flip_Flop d_ff_3 (.clk(clock_1_out), .D(d_ff_2_q), .Q(d_ff_3_q));  // open: Qn, preset, en, reset
  T_Flip_Flop t_ff_2 (.clk(t_ff_1_q), .T(in_4), .Q(out_7));  // open: Qn, preset, reset, en
  D_Flip_Flop d_ff_4 (.clk(clock_1_out), .D(d_ff_3_q));  // open: Q, Qn, preset, en, reset

  // Notes on the sheet:
  //   SR Latch
  //   Frequency Divider
  //   Shift Register
endmodule
