// Logisim project digital-hw-2b.circ as structural Verilog: 1 circuit, main circuit main
module main (
  input  A,
  input  B,
  output Q
);

  wire nand_1_out, nand_2_out, nand_3_out;

  nand nand_1 (nand_1_out, ~B, ~A);  // NAND_Gate
  nand nand_2 (nand_2_out, B, A);
  nand nand_3 (nand_3_out, Q, nand_1_out);
  nand nand_4 (Q, nand_3_out, nand_2_out);
endmodule
