// Logisim project digital-hw-2e.circ as structural Verilog: 1 circuit, main circuit main
module main (
  input  A,
  input  B,
  output Q
);

  wire nor_1_out, nor_2_out, nor_3_out;

  nor nor_1 (nor_1_out, Q, A);
  nor nor_2 (nor_2_out, Q, B);
  nor nor_3 (nor_3_out, B, A);
  nor nor_4 (Q, nor_1_out, nor_2_out, nor_3_out);
endmodule
