// Logisim project digital-hw-3b.circ as structural Verilog: 1 circuit, main circuit main
module main (
  output out_1,
  output out_2,
  output out_3
);

  wire and_1_out, and_2_out, and_3_out, and_4_out, clock_1_out, or_1_out, or_2_out, or_3_out, xnor_1_out,
       xor_1_out, xor_2_out, xor_3_out;

  and and_1 (and_1_out, ~out_2, ~out_3);  // AND_Gate
  and and_2 (and_2_out, out_2, ~out_3);  // AND_Gate
  or or_1 (or_1_out, and_2_out, and_3_out);
  and and_3 (and_3_out, out_1, out_3);
  and and_4 (and_4_out, out_2, ~out_3);  // AND_Gate
  or or_2 (or_2_out, and_4_out, ~out_1);  // OR_Gate
  or or_3 (or_3_out, and_1_out, xnor_1_out);
  xnor xnor_1 (xnor_1_out, out_1, out_2);
  xor xor_1 (xor_1_out, or_1_out, out_1);
  xor xor_2 (xor_2_out, or_2_out, out_2);
  xor xor_3 (xor_3_out, or_3_out, out_3);
  Clock clock_1 (.out(clock_1_out));
  T_Flip_Flop t_ff_1 (.clk(clock_1_out), .T(xor_1_out), .Q(out_1));  // open: Qn, preset, reset, en
  T_Flip_Flop t_ff_2 (.clk(clock_1_out), .T(xor_2_out), .Q(out_2));  // open: Qn, preset, reset, en
  T_Flip_Flop t_ff_3 (.clk(clock_1_out), .T(xor_3_out), .Q(out_3));  // open: Qn, preset, reset, en
endmodule
